// Logisim project calculatorCPU.circ as structural Verilog: 19 circuits, main circuit main
module main (
);

  wire _0_out, _1_out, _2_out, _3_out, _4_out, _5_out, _6_out, _7_out, _8_out, _9_out, button_2_out,
       button_3_out, button_4_out, button_5_out, button_out, C_out, keypad_controller_1_write;
  wire [2:0] lcd_controller_1__7_segment_3_2, lcd_controller_1__7_segment_4_2,
       lcd_controller_1__7_segment_5_2, lcd_controller_1__7_segment_6_2, lcd_controller_1__7_segment_7_2,
       lcd_controller_1__7_segment_8_2, lcd_controller_1__7_segment_9_2, lcd_controller_1_minus_2;
  wire [3:0] lcd_controller_1__7_segment_3, lcd_controller_1__7_segment_4, lcd_controller_1__7_segment_5,
       lcd_controller_1__7_segment_6, lcd_controller_1__7_segment_7, lcd_controller_1__7_segment_8,
       lcd_controller_1__7_segment_9, lcd_controller_1_minus;
  wire [6:0] lcd_controller_1__7_segment_0, lcd_controller_1__7_segment_1, lcd_controller_1__7_segment_2;
  wire [31:0] cpu_1_from__t8, cpu_1_from__t94, keypad_controller_1_output;

  CPU cpu_1 (
    .Write_to__t9(keypad_controller_1_output), .Write_To_Keyboard(keypad_controller_1_write),
    .from__t8(cpu_1_from__t8), .from__t94(cpu_1_from__t94));
  _7_Segment_Display u_7_segment_display_1 (
    .g(lcd_controller_1__7_segment_9[0]), .f(lcd_controller_1__7_segment_9[1]),
    .a(lcd_controller_1__7_segment_9[2]), .b(lcd_controller_1__7_segment_9[3]),
    .e(lcd_controller_1__7_segment_9_2[0]), .d(lcd_controller_1__7_segment_9_2[1]),
    .c(lcd_controller_1__7_segment_9_2[2]));  // open: dp
  _7_Segment_Display u_7_segment_display_2 (
    .g(lcd_controller_1_minus[0]), .f(lcd_controller_1_minus[1]), .a(lcd_controller_1_minus[2]),
    .b(lcd_controller_1_minus[3]), .e(lcd_controller_1_minus_2[0]), .d(lcd_controller_1_minus_2[1]),
    .c(lcd_controller_1_minus_2[2]));  // open: dp
  LCD_Controller lcd_controller_1 (
    .From__t8(cpu_1_from__t8), .Minus({lcd_controller_1_minus_2, lcd_controller_1_minus}),
    ._7_Segment_9({lcd_controller_1__7_segment_9_2, lcd_controller_1__7_segment_9}),
    ._7_Segment_8({lcd_controller_1__7_segment_8_2, lcd_controller_1__7_segment_8}),
    ._7_Segment_7({lcd_controller_1__7_segment_7_2, lcd_controller_1__7_segment_7}),
    ._7_Segment_6({lcd_controller_1__7_segment_6_2, lcd_controller_1__7_segment_6}),
    ._7_Segment_5({lcd_controller_1__7_segment_5_2, lcd_controller_1__7_segment_5}),
    ._7_Segment_4({lcd_controller_1__7_segment_4_2, lcd_controller_1__7_segment_4}),
    ._7_Segment_3({lcd_controller_1__7_segment_3_2, lcd_controller_1__7_segment_3}),
    ._7_Segment_2(lcd_controller_1__7_segment_2), ._7_Segment_1(lcd_controller_1__7_segment_1),
    ._7_Segment_0(lcd_controller_1__7_segment_0));
  Keypad_Controller keypad_controller_1 (
    .C(C_out), .in_2(button_out), .in_3(button_5_out), .in_4(button_4_out), .in_5(button_3_out),
    .in_6(button_2_out), ._9(_9_out), ._8(_8_out), ._7(_7_out), ._6(_6_out), ._5(_5_out), ._4(_4_out),
    ._3(_3_out), ._2(_2_out), ._1(_1_out), ._0(_0_out), .From__t9(cpu_1_from__t94),
    .Write(keypad_controller_1_write), .Output(keypad_controller_1_output));
  _7_Segment_Display u_7_segment_display_3 (
    .g(lcd_controller_1__7_segment_7[0]), .f(lcd_controller_1__7_segment_7[1]),
    .a(lcd_controller_1__7_segment_7[2]), .b(lcd_controller_1__7_segment_7[3]),
    .e(lcd_controller_1__7_segment_7_2[0]), .d(lcd_controller_1__7_segment_7_2[1]),
    .c(lcd_controller_1__7_segment_7_2[2]));  // open: dp
  _7_Segment_Display u_7_segment_display_4 (
    .g(lcd_controller_1__7_segment_8[0]), .f(lcd_controller_1__7_segment_8[1]),
    .a(lcd_controller_1__7_segment_8[2]), .b(lcd_controller_1__7_segment_8[3]),
    .e(lcd_controller_1__7_segment_8_2[0]), .d(lcd_controller_1__7_segment_8_2[1]),
    .c(lcd_controller_1__7_segment_8_2[2]));  // open: dp
  _7_Segment_Display u_7_segment_display_5 (
    .g(lcd_controller_1__7_segment_5[0]), .f(lcd_controller_1__7_segment_5[1]),
    .a(lcd_controller_1__7_segment_5[2]), .b(lcd_controller_1__7_segment_5[3]),
    .e(lcd_controller_1__7_segment_5_2[0]), .d(lcd_controller_1__7_segment_5_2[1]),
    .c(lcd_controller_1__7_segment_5_2[2]));  // open: dp
  _7_Segment_Display u_7_segment_display_6 (
    .g(lcd_controller_1__7_segment_6[0]), .f(lcd_controller_1__7_segment_6[1]),
    .a(lcd_controller_1__7_segment_6[2]), .b(lcd_controller_1__7_segment_6[3]),
    .e(lcd_controller_1__7_segment_6_2[0]), .d(lcd_controller_1__7_segment_6_2[1]),
    .c(lcd_controller_1__7_segment_6_2[2]));  // open: dp
  Button _7 (.out(_7_out));
  Button _4 (.out(_4_out));
  Button _1 (.out(_1_out));
  Button _0 (.out(_0_out));
  _7_Segment_Display u_7_segment_display_7 (
    .g(lcd_controller_1__7_segment_3[0]), .f(lcd_controller_1__7_segment_3[1]),
    .a(lcd_controller_1__7_segment_3[2]), .b(lcd_controller_1__7_segment_3[3]),
    .e(lcd_controller_1__7_segment_3_2[0]), .d(lcd_controller_1__7_segment_3_2[1]),
    .c(lcd_controller_1__7_segment_3_2[2]));  // open: dp
  _7_Segment_Display u_7_segment_display_8 (
    .g(lcd_controller_1__7_segment_4[0]), .f(lcd_controller_1__7_segment_4[1]),
    .a(lcd_controller_1__7_segment_4[2]), .b(lcd_controller_1__7_segment_4[3]),
    .e(lcd_controller_1__7_segment_4_2[0]), .d(lcd_controller_1__7_segment_4_2[1]),
    .c(lcd_controller_1__7_segment_4_2[2]));  // open: dp
  Button _8 (.out(_8_out));
  Button _5 (.out(_5_out));
  Button _2 (.out(_2_out));
  Button C (.out(C_out));
  _7_Segment_Display u_7_segment_display_9 (
    .g(lcd_controller_1__7_segment_1[0]), .f(lcd_controller_1__7_segment_1[1]),
    .a(lcd_controller_1__7_segment_1[2]), .b(lcd_controller_1__7_segment_1[3]),
    .e(lcd_controller_1__7_segment_1[4]), .d(lcd_controller_1__7_segment_1[5]),
    .c(lcd_controller_1__7_segment_1[6]));  // open: dp
  _7_Segment_Display u_7_segment_display_10 (
    .g(lcd_controller_1__7_segment_2[0]), .f(lcd_controller_1__7_segment_2[1]),
    .a(lcd_controller_1__7_segment_2[2]), .b(lcd_controller_1__7_segment_2[3]),
    .e(lcd_controller_1__7_segment_2[4]), .d(lcd_controller_1__7_segment_2[5]),
    .c(lcd_controller_1__7_segment_2[6]));  // open: dp
  Button _9 (.out(_9_out));
  Button _6 (.out(_6_out));
  Button _3 (.out(_3_out));
  Button button (.out(button_out));
  _7_Segment_Display u_7_segment_display_11 (
    .g(lcd_controller_1__7_segment_0[0]), .f(lcd_controller_1__7_segment_0[1]),
    .a(lcd_controller_1__7_segment_0[2]), .b(lcd_controller_1__7_segment_0[3]),
    .e(lcd_controller_1__7_segment_0[4]), .d(lcd_controller_1__7_segment_0[5]),
    .c(lcd_controller_1__7_segment_0[6]));  // open: dp
  Button button_2 (.out(button_2_out));
  Button button_3 (.out(button_3_out));
  Button button_4 (.out(button_4_out));
  Button button_5 (.out(button_5_out));

  // Notes on the sheet:
  //   From $t8
  //   From $t9
  //   Write Data to $t9
  //   Write Signal for $t9
endmodule

module LCD_Controller (
  input  [31:0] From__t8,
  output [6:0] Minus,
  output [6:0] _7_Segment_9,
  output [6:0] _7_Segment_8,
  output [6:0] _7_Segment_7,
  output [6:0] _7_Segment_6,
  output [6:0] _7_Segment_5,
  output [6:0] _7_Segment_4,
  output [6:0] _7_Segment_3,
  output [6:0] _7_Segment_2,
  output [6:0] _7_Segment_1,
  output [6:0] _7_Segment_0
);

  wire [3:0] binarytobcd_1_bcd0, binarytobcd_1_bcd1, binarytobcd_1_bcd2, binarytobcd_1_bcd3,
       binarytobcd_1_bcd4, binarytobcd_1_bcd5, binarytobcd_1_bcd6, binarytobcd_1_bcd7, binarytobcd_1_bcd8,
       binarytobcd_1_bcd9;

  BinaryToBCD binarytobcd_1 (
    .Input(From__t8), .Minus(Minus[0]), .BCD9(binarytobcd_1_bcd9), .BCD8(binarytobcd_1_bcd8),
    .BCD7(binarytobcd_1_bcd7), .BCD6(binarytobcd_1_bcd6), .BCD5(binarytobcd_1_bcd5),
    .BCD4(binarytobcd_1_bcd4), .BCD3(binarytobcd_1_bcd3), .BCD2(binarytobcd_1_bcd2),
    .BCD1(binarytobcd_1_bcd1), .BCD0(binarytobcd_1_bcd0));
  _7_Segment_Controller u_7_segment_controller_1 (.BCD(binarytobcd_1_bcd9), .out_2(_7_Segment_9));
  _7_Segment_Controller u_7_segment_controller_2 (.BCD(binarytobcd_1_bcd8), .out_2(_7_Segment_8));
  _7_Segment_Controller u_7_segment_controller_3 (.BCD(binarytobcd_1_bcd7), .out_2(_7_Segment_7));
  _7_Segment_Controller u_7_segment_controller_4 (.BCD(binarytobcd_1_bcd6), .out_2(_7_Segment_6));
  _7_Segment_Controller u_7_segment_controller_5 (.BCD(binarytobcd_1_bcd5), .out_2(_7_Segment_5));
  _7_Segment_Controller u_7_segment_controller_6 (.BCD(binarytobcd_1_bcd4), .out_2(_7_Segment_4));
  _7_Segment_Controller u_7_segment_controller_7 (.BCD(binarytobcd_1_bcd3), .out_2(_7_Segment_3));
  _7_Segment_Controller u_7_segment_controller_8 (.BCD(binarytobcd_1_bcd2), .out_2(_7_Segment_2));
  _7_Segment_Controller u_7_segment_controller_9 (.BCD(binarytobcd_1_bcd1), .out_2(_7_Segment_1));
  _7_Segment_Controller u_7_segment_controller_10 (.BCD(binarytobcd_1_bcd0), .out_2(_7_Segment_0));

  assign Minus[6:1] = {6{1'b0}};
endmodule

module _7_Segment_Controller (
  input  [3:0] BCD,
  output [6:0] out_2
);

  wire and_1_out, and_2_out, and_3_out, and_4_out, and_5_out, and_6_out, and_7_out, and_8_out, and_9_out,
       and_10_out, and_11_out, and_12_out, and_13_out, and_14_out, and_15_out, and_16_out, not_1_out,
       not_2_out, not_3_out, not_4_out, not_5_out, not_6_out, not_7_out, not_8_out, not_9_out, not_10_out,
       not_11_out, not_12_out, not_13_out, not_14_out, not_15_out, not_16_out, not_17_out, not_18_out,
       not_19_out, not_20_out, not_21_out;

  not not_1 (not_1_out, BCD[2]);
  not not_2 (not_2_out, BCD[0]);
  not not_3 (not_3_out, BCD[1]);
  not not_4 (not_4_out, BCD[1]);
  not not_5 (not_5_out, BCD[0]);
  not not_6 (not_6_out, BCD[1]);
  not not_7 (not_7_out, BCD[0]);
  not not_8 (not_8_out, BCD[2]);
  not not_9 (not_9_out, BCD[0]);
  not not_10 (not_10_out, BCD[1]);
  not not_11 (not_11_out, BCD[0]);
  not not_12 (not_12_out, BCD[2]);
  not not_13 (not_13_out, BCD[0]);
  not not_14 (not_14_out, BCD[0]);
  not not_15 (not_15_out, BCD[2]);
  not not_16 (not_16_out, BCD[0]);
  not not_17 (not_17_out, BCD[2]);
  not not_18 (not_18_out, BCD[0]);
  not not_19 (not_19_out, BCD[1]);
  not not_20 (not_20_out, BCD[1]);
  and and_1 (and_1_out, not_1_out, BCD[1]);
  and and_2 (and_2_out, BCD[1], not_2_out);
  and and_3 (and_3_out, BCD[2], not_3_out);
  and and_4 (and_4_out, not_4_out, not_5_out);
  and and_5 (and_5_out, BCD[2], not_6_out);
  and and_6 (and_6_out, BCD[2], not_7_out);
  and and_7 (and_7_out, not_8_out, not_9_out);
  and and_8 (and_8_out, BCD[2], BCD[0]);
  not not_21 (not_21_out, BCD[2]);
  and and_9 (and_9_out, not_10_out, not_11_out);
  and and_10 (and_10_out, BCD[1], BCD[0]);
  and and_11 (and_11_out, not_12_out, not_13_out);
  and and_12 (and_12_out, BCD[1], not_14_out);
  and and_13 (and_13_out, not_15_out, not_16_out);
  and and_14 (and_14_out, not_17_out, BCD[1]);
  and and_15 (and_15_out, BCD[1], not_18_out);
  and and_16 (and_16_out, BCD[2], not_19_out, BCD[0]);
  or or_1 (out_2[6], not_20_out, BCD[0], BCD[2]);
  or or_2 (out_2[0], and_1_out, and_2_out, and_3_out, BCD[3]);
  or or_3 (out_2[1], and_4_out, and_5_out, and_6_out, BCD[3]);
  or or_4 (out_2[2], and_7_out, BCD[1], and_8_out, BCD[3]);
  or or_5 (out_2[3], not_21_out, and_9_out, and_10_out);
  or or_6 (out_2[4], and_11_out, and_12_out);
  or or_7 (out_2[5], and_13_out, and_14_out, and_15_out, and_16_out);
endmodule

module BinaryToBCD (
  input  [31:0] Input,
  output Minus,
  output [3:0] BCD9,
  output [3:0] BCD8,
  output [3:0] BCD7,
  output [3:0] BCD6,
  output [3:0] BCD5,
  output [3:0] BCD4,
  output [3:0] BCD3,
  output [3:0] BCD2,
  output [3:0] BCD1,
  output [3:0] BCD0
);

  wire [27:0] subtractor_1_out, subtractor_2_out, subtractor_3_out, subtractor_4_out, subtractor_5_out,
       subtractor_6_out, subtractor_7_out, subtractor_8_out, subtractor_9_out;
  wire [31:0] adder_1_out, divider_1_out, divider_2_out, divider_3_out, divider_4_out, divider_5_out,
       divider_6_out, divider_7_out, divider_8_out, multiplexer_1_out, multiplier_1_out, multiplier_2_out,
       multiplier_3_out, multiplier_4_out, multiplier_5_out, multiplier_6_out, multiplier_7_out,
       multiplier_8_out, multiplier_9_out, not_1_out;
  wire [31:4] divider_9_out;

  assign not_1_out = ~Input;  // NOT_Gate not_1, 32 bits wide
  Adder #(.width(32)) adder_1 (.a(not_1_out), .b(32'h1), .out(adder_1_out));  // open: cin, cout
  Multiplexer #(.width(32)) multiplexer_1 (
    .in0(Input), .in1(adder_1_out), .out(multiplexer_1_out), .sel(Input[31]));  // open: en
  Subtractor #(.width(32)) subtractor_1 (
    .a(multiplexer_1_out), .b(multiplier_1_out), .out({subtractor_1_out, BCD0}));  // open: bin, bout
  Multiplier #(.width(32)) multiplier_1 (.a(divider_1_out), .b(32'ha), .out(multiplier_1_out));  // open: cin, cout
  Divider #(.width(32)) divider_1 (.a(multiplexer_1_out), .b(32'ha), .out(divider_1_out));  // open: upper, rem
  Subtractor #(.width(32)) subtractor_2 (
    .a(divider_1_out), .b(multiplier_2_out), .out({subtractor_2_out, BCD1}));  // open: bin, bout
  Multiplier #(.width(32)) multiplier_2 (.a(divider_2_out), .b(32'ha), .out(multiplier_2_out));  // open: cin, cout
  Divider #(.width(32)) divider_2 (.a(divider_1_out), .b(32'ha), .out(divider_2_out));  // open: upper, rem
  Subtractor #(.width(32)) subtractor_3 (
    .a(divider_2_out), .b(multiplier_3_out), .out({subtractor_3_out, BCD2}));  // open: bin, bout
  Multiplier #(.width(32)) multiplier_3 (.a(divider_3_out), .b(32'ha), .out(multiplier_3_out));  // open: cin, cout
  Divider #(.width(32)) divider_3 (.a(divider_2_out), .b(32'ha), .out(divider_3_out));  // open: upper, rem
  Subtractor #(.width(32)) subtractor_4 (
    .a(divider_3_out), .b(multiplier_4_out), .out({subtractor_4_out, BCD3}));  // open: bin, bout
  Multiplier #(.width(32)) multiplier_4 (.a(divider_4_out), .b(32'ha), .out(multiplier_4_out));  // open: cin, cout
  Divider #(.width(32)) divider_4 (.a(divider_3_out), .b(32'ha), .out(divider_4_out));  // open: upper, rem
  Subtractor #(.width(32)) subtractor_5 (
    .a(divider_4_out), .b(multiplier_5_out), .out({subtractor_5_out, BCD4}));  // open: bin, bout
  Multiplier #(.width(32)) multiplier_5 (.a(divider_5_out), .b(32'ha), .out(multiplier_5_out));  // open: cin, cout
  Divider #(.width(32)) divider_5 (.a(divider_4_out), .b(32'ha), .out(divider_5_out));  // open: upper, rem
  Subtractor #(.width(32)) subtractor_6 (
    .a(divider_5_out), .b(multiplier_6_out), .out({subtractor_6_out, BCD5}));  // open: bin, bout
  Multiplier #(.width(32)) multiplier_6 (.a(divider_6_out), .b(32'ha), .out(multiplier_6_out));  // open: cin, cout
  Divider #(.width(32)) divider_6 (.a(divider_5_out), .b(32'ha), .out(divider_6_out));  // open: upper, rem
  Subtractor #(.width(32)) subtractor_7 (
    .a(divider_6_out), .b(multiplier_7_out), .out({subtractor_7_out, BCD6}));  // open: bin, bout
  Multiplier #(.width(32)) multiplier_7 (.a(divider_7_out), .b(32'ha), .out(multiplier_7_out));  // open: cin, cout
  Divider #(.width(32)) divider_7 (.a(divider_6_out), .b(32'ha), .out(divider_7_out));  // open: upper, rem
  Subtractor #(.width(32)) subtractor_8 (
    .a(divider_7_out), .b(multiplier_8_out), .out({subtractor_8_out, BCD7}));  // open: bin, bout
  Multiplier #(.width(32)) multiplier_8 (.a(divider_8_out), .b(32'ha), .out(multiplier_8_out));  // open: cin, cout
  Divider #(.width(32)) divider_8 (.a(divider_7_out), .b(32'ha), .out(divider_8_out));  // open: upper, rem
  Subtractor #(.width(32)) subtractor_9 (
    .a(divider_8_out), .b(multiplier_9_out), .out({subtractor_9_out, BCD8}));  // open: bin, bout
  Multiplier #(.width(32)) multiplier_9 (
    .a({divider_9_out, BCD9}), .b(32'ha), .out(multiplier_9_out));  // open: cin, cout
  Divider #(.width(32)) divider_9 (.a(divider_8_out), .b(32'ha), .out({divider_9_out, BCD9}));  // open: upper, rem

  assign Minus = Input[31];
endmodule

module Keypad_Controller (
  input  C,
  input  in_2,
  input  in_3,
  input  in_4,
  input  in_5,
  input  in_6,
  input  _9,
  input  _8,
  input  _7,
  input  _6,
  input  _5,
  input  _4,
  input  _3,
  input  _2,
  input  _1,
  input  _0,
  input  [31:0] From__t9,
  output Write,
  output [31:0] Output
);

  wire iszero_1_out_2, iszero_2_out_2;
  wire [3:0] or_4_out;
  wire [15:0] and_1_out;

  and and_1 (and_1_out[0], iszero_1_out_2, C);
  and and_2 (and_1_out[1], in_2, iszero_1_out_2);
  and and_3 (and_1_out[2], in_3, iszero_1_out_2);
  and and_4 (and_1_out[3], in_4, iszero_1_out_2);
  and and_5 (and_1_out[4], iszero_1_out_2, in_5);
  and and_6 (and_1_out[5], in_6, iszero_1_out_2);
  and and_7 (and_1_out[6], _9, iszero_1_out_2);
  and and_8 (and_1_out[7], _8, iszero_1_out_2);
  and and_9 (and_1_out[8], iszero_1_out_2, _7);
  and and_10 (and_1_out[9], _6, iszero_1_out_2);
  and and_11 (and_1_out[10], iszero_1_out_2, _5);
  and and_12 (and_1_out[11], iszero_1_out_2, _4);
  and and_13 (and_1_out[12], iszero_1_out_2, _3);
  and and_14 (and_1_out[13], iszero_1_out_2, _2);
  and and_15 (and_1_out[14], iszero_1_out_2, _1);
  and and_16 (and_1_out[15], _0, iszero_1_out_2);
  isZero iszero_1 (.Input(From__t9), .out_2(iszero_1_out_2));
  or or_1 (or_4_out[3], and_1_out[0], and_1_out[1], and_1_out[2], and_1_out[3], and_1_out[4], and_1_out[5], and_1_out[6], and_1_out[7]);
  or or_2 (or_4_out[2], and_1_out[8], and_1_out[9], and_1_out[10], and_1_out[11], and_1_out[0], and_1_out[1], and_1_out[2], and_1_out[3]);
  or or_3 (or_4_out[1], and_1_out[12], and_1_out[13], and_1_out[9], and_1_out[8], and_1_out[5], and_1_out[4], and_1_out[1], and_1_out[0]);
  or or_4 (or_4_out[0], and_1_out[12], and_1_out[14], and_1_out[10], and_1_out[8], and_1_out[6], and_1_out[4], and_1_out[2], and_1_out[0]);
  isZero iszero_2 (.Input({{16{1'b0}}, and_1_out}), .out_2(iszero_2_out_2));
  not not_1 (Write, iszero_2_out_2);
  assign Output = Write ? {28'h8000000, or_4_out} : 32'bz;  // Controlled_Buffer controlled_buffer_1
endmodule

module isZero (
  input  [31:0] Input,
  output out_2
);

  wire or_1_out;

  not not_1 (out_2, or_1_out);
  or or_1 (or_1_out, Input[0], Input[1], Input[2], Input[3], Input[4], Input[5], Input[6], Input[7], Input[8], Input[9], Input[10], Input[11], Input[12], Input[13], Input[14], Input[15], Input[16], Input[17], Input[18], Input[19], Input[20], Input[21], Input[22], Input[23], Input[24], Input[25], Input[26], Input[27], Input[28], Input[29], Input[30], Input[31]);
endmodule

module Instruction_Memory__Done (
  input  [15:0] Adress,
  output [31:0] out_2
);

  ROM #(.addrWidth(16), .dataWidth(32)) rom_1 (.addr(Adress), .data(out_2), .sel(1'b1));

  // Notes on the sheet:
  //   contents of rom_1 (hex, n*v repeats v):
  //   4820 5020 4020 120c020 c820 1320ffff 19c840 19c842 2001000e 10390029 2001000f 1039fff4 2b2b000a
  //   15600002 2b2b000e 15600007 96040 968c0 1ac4820 1394820 120c020 c820 8100005 194020 120c020 c820
  //   1320ffff 8100021 194020 120c020 c820 1320ffff 8100021 1320ffff 19c840 19c842 2001000e 1039000d
  //   2001000f 1039ffd8 2b2b000a 15600002 2b2b000e 1560fff0 a6040 a68c0 18d5020 1595020 140c020 c820
  //   8100037 1208820 220c020 c820 81000fe 1320ffff 19c840 19c842 2001000e 1039006d 2001000f 1039ffc2
  //   2b2b000a 15600002 2b2b000e 15600007 a6040 a68c0 18d5020 1595020 140c020 c820 8100037 2001000a
  //   10280006 2001000b 1028000b 2001000c 10280010 2001000d 1028002a 12a8820 220c020 2204820 5020 3204020
  //   c820 8100021 12a8822 220c020 2204820 3204020 5020 c820 8100021 1140003b 1120003a 200e0001 114e003f
  //   7020 200e0001 1ca9024 8820 1409820 139842 139840 12400001 1208820 21ef0002 9a040 2918820 166ffffc
  //   2204820 3204020 9820 9020 7820 c820 9020 a020 5020 220c020 8100021 11400078 11200077 120702a
  //   11c00002 94822 20140001 8820 7820 200e0001 1ca9024 8820 12400001 1208822 21ef0001 12a4822 12a982a
  //   1260fffc 1e08820 9820 9020 7820 c820 2204820 3204020 220c020 1280ff8c 118822 220c020 2204820 3204020
  //   5020 8100021 c020 8820 3204020 2204820 5020 c820 8100021 1208820 114820 220c020 5020 3204020 c820
  //   8100021 2001000a 10280006 2001000b 10280009 2001000c 1028000c 2001000d 10280025 12a8820 220c020 c820
  //   5020 81000fe 12a8822 220c020 c820 5020 81000fe 11400038 11200037 200e0001 114e003a 7020 200e0001
  //   1ca9024 8820 1409820 139842 139840 12400001 1208820 20150002 1f57820 9a040 2918820 166ffffb 9820
  //   9020 7820 c820 9020 a020 5020 220c020 81000fe 1140001d 1120001c 120702a 11c00002 94822 20140001 8820
  //   7820 200e0001 1ca9024 8820 12400001 1208822 20150001 1f57820 12a4822 12a982a 1260fffb 1e08820 9820
  //   9020 7820 c820 9020 220c020 1280000e 118822 220c020 5020 81000fe c020 8820 c820 5020 81000fe 1208820
  //   220c020 c820 5020 81000fe 1320ffff 19c840 19c842 2001000f 1039fefd 2001000e 10390009 2b2b000a
  //   1560000a 2b2b000e 15600000 194020 2204820 5020 c820 8100021 220c020 c820 81000fe 3204820 120c020
  //   c820 8100005
endmodule

module _32_bit_ALU__Done (
  input  [1:0] OP,
  input  A_Invert,
  input  BInvert,
  input  [31:0] A_Input,
  input  [31:0] B_Input,
  input  [1:0] Shift_Control,
  input  [4:0] Shift_Amount,
  output Zero,
  output [31:0] Result,
  output Overflow
);

  wire n8_bit_alu_1_carry_out, n8_bit_alu_2_carry_out, n8_bit_alu_3_carry_out, n8_bit_alu_4_set, undriven;
  wire [7:0] n8_bit_alu_1_result, n8_bit_alu_2_result, n8_bit_alu_3_result, n8_bit_alu_4_result;
  wire [31:0] shifter_1_out, shifter_2_out;

  // Probe on undriven
  _8_bit_ALU u_8_bit_alu_1 (
    .A(A_Input[7:0]), .B(B_Input[7:0]), .Less(n8_bit_alu_4_set), .A_Invert(A_Invert), .BInvert(BInvert),
    .Carry_In(BInvert), .OP(OP), .Carry_Out(n8_bit_alu_1_carry_out), .Result(n8_bit_alu_1_result));  // open: Set
  _8_bit_ALU u_8_bit_alu_2 (
    .A(A_Input[15:8]), .B(B_Input[15:8]), .Less(1'b0), .A_Invert(A_Invert), .BInvert(BInvert),
    .Carry_In(n8_bit_alu_1_carry_out), .OP(OP), .Carry_Out(n8_bit_alu_2_carry_out),
    .Result(n8_bit_alu_2_result));  // open: Set
  _8_bit_ALU u_8_bit_alu_3 (
    .A(A_Input[23:16]), .B(B_Input[23:16]), .Less(1'b0), .A_Invert(A_Invert), .BInvert(BInvert),
    .Carry_In(n8_bit_alu_2_carry_out), .OP(OP), .Carry_Out(n8_bit_alu_3_carry_out),
    .Result(n8_bit_alu_3_result));  // open: Set
  _8_bit_ALU u_8_bit_alu_4 (
    .A(A_Input[31:24]), .B(B_Input[31:24]), .Less(1'b0), .A_Invert(A_Invert), .BInvert(BInvert),
    .Carry_In(n8_bit_alu_3_carry_out), .OP(OP), .Carry_Out(Overflow), .Result(n8_bit_alu_4_result),
    .Set(n8_bit_alu_4_set));
  Shifter #(.width(32)) shifter_1 (.in(B_Input), .\dist (Shift_Amount), .out(shifter_1_out));
  Shifter #(.width(32), .shift("lr")) shifter_2 (.in(B_Input), .\dist (Shift_Amount), .out(shifter_2_out));
  Multiplexer #(.select(2), .width(32)) multiplexer_1 (
    .in0({n8_bit_alu_4_result, n8_bit_alu_3_result, n8_bit_alu_2_result, n8_bit_alu_1_result}),
    .in1(shifter_1_out), .in2(shifter_2_out), .out(Result), .sel(Shift_Control));  // open: in3, en
  nor nor_1 (Zero, n8_bit_alu_4_result[0], n8_bit_alu_4_result[1], n8_bit_alu_4_result[2], n8_bit_alu_4_result[3], n8_bit_alu_4_result[4], n8_bit_alu_4_result[5], n8_bit_alu_4_result[6], n8_bit_alu_4_result[7], n8_bit_alu_1_result[0], n8_bit_alu_1_result[1], n8_bit_alu_1_result[2], n8_bit_alu_1_result[3], n8_bit_alu_1_result[4], n8_bit_alu_1_result[5], n8_bit_alu_1_result[6], n8_bit_alu_1_result[7], n8_bit_alu_2_result[0], n8_bit_alu_2_result[1], n8_bit_alu_2_result[2], n8_bit_alu_2_result[3], n8_bit_alu_2_result[4], n8_bit_alu_2_result[5], n8_bit_alu_2_result[6], n8_bit_alu_2_result[7], n8_bit_alu_3_result[0], n8_bit_alu_3_result[1], n8_bit_alu_3_result[2], n8_bit_alu_3_result[3], n8_bit_alu_3_result[4], n8_bit_alu_3_result[5], n8_bit_alu_3_result[6], n8_bit_alu_3_result[7]);
endmodule

module Register_File__Finish__t8___t9 (
  input  Write,
  input  [4:0] Write_Register,
  input  [31:0] Write_Data,
  input  [4:0] Read_Register_1,
  input  [4:0] Read_Register_2,
  input  [31:0] Write_to__t9,
  input  Write_Signal_From_Keypad,
  input  Clock,
  output [31:0] Read_Data_1,
  output [31:0] Read_Data_2,
  output [31:0] from__t8,
  output [31:0] from__t9
);

  wire controlled_buffer_2_out, demultiplexer_1_out0, demultiplexer_1_out1, demultiplexer_1_out2,
       demultiplexer_1_out3, demultiplexer_1_out4, demultiplexer_1_out5, demultiplexer_1_out6,
       demultiplexer_1_out7, demultiplexer_1_out8, demultiplexer_1_out9, demultiplexer_1_out10,
       demultiplexer_1_out11, demultiplexer_1_out12, demultiplexer_1_out13, demultiplexer_1_out14,
       demultiplexer_1_out15, demultiplexer_1_out16, demultiplexer_1_out17, demultiplexer_1_out18,
       demultiplexer_1_out19, demultiplexer_1_out20, demultiplexer_1_out21, demultiplexer_1_out22,
       demultiplexer_1_out23, demultiplexer_1_out24, demultiplexer_1_out25, demultiplexer_1_out26,
       demultiplexer_1_out27, demultiplexer_1_out28, demultiplexer_1_out29, demultiplexer_1_out30,
       demultiplexer_1_out31;
  wire [31:0] controlled_buffer_1_out, Reg_0_q, Reg_1_q, Reg_2_q, Reg_3_q, Reg_4_q, Reg_5_q, Reg_6_q,
       Reg_7_q, Reg_8_q, Reg_9_q, Reg_10_q, Reg_11_q, Reg_12_q, Reg_13_q, Reg_14_q, Reg_15_q, Reg_16_q,
       Reg_17_q, Reg_18_q, Reg_19_q, Reg_20_q, Reg_21_q, Reg_22_q, Reg_23_q, Reg_26_q, Reg_27_q, Reg_28_q,
       Reg_29_q, Reg_30_q, Reg_31_q;

  _32_bit_ALU__Done u_32_bit_alu_done_1 ();  // open: A_Input, B_Input, Shift_Amount, A_Invert, BInvert, OP, Shift_Control, Zero, Result, Overflow
  Demultiplexer #(.select(5)) demultiplexer_1 (
    .out0(demultiplexer_1_out0), .out1(demultiplexer_1_out1), .out2(demultiplexer_1_out2),
    .out3(demultiplexer_1_out3), .out4(demultiplexer_1_out4), .out5(demultiplexer_1_out5),
    .out6(demultiplexer_1_out6), .out7(demultiplexer_1_out7), .out8(demultiplexer_1_out8),
    .out9(demultiplexer_1_out9), .out10(demultiplexer_1_out10), .out11(demultiplexer_1_out11),
    .out12(demultiplexer_1_out12), .out13(demultiplexer_1_out13), .out14(demultiplexer_1_out14),
    .out15(demultiplexer_1_out15), .out16(demultiplexer_1_out16), .out17(demultiplexer_1_out17),
    .out18(demultiplexer_1_out18), .out19(demultiplexer_1_out19), .out20(demultiplexer_1_out20),
    .out21(demultiplexer_1_out21), .out22(demultiplexer_1_out22), .out23(demultiplexer_1_out23),
    .out24(demultiplexer_1_out24), .out25(demultiplexer_1_out25), .out26(demultiplexer_1_out26),
    .out27(demultiplexer_1_out27), .out28(demultiplexer_1_out28), .out29(demultiplexer_1_out29),
    .out30(demultiplexer_1_out30), .out31(demultiplexer_1_out31), .in(Write), .sel(Write_Register));  // open: en
  assign controlled_buffer_1_out = Write_Signal_From_Keypad ? Write_to__t9 : 32'bz;  // Controlled_Buffer controlled_buffer_1
  assign controlled_buffer_2_out = Write_Signal_From_Keypad ? Write_Signal_From_Keypad : 1'bz;  // Controlled_Buffer controlled_buffer_2
  assign controlled_buffer_1_out = demultiplexer_1_out25 ? Write_Data : 32'bz;  // Controlled_Buffer controlled_buffer_3
  assign controlled_buffer_2_out = demultiplexer_1_out25 ? demultiplexer_1_out25 : 1'bz;  // Controlled_Buffer controlled_buffer_4
  Register #(.width(32), .trigger("falling")) Reg_0 (
    .D(Write_Data), .en(demultiplexer_1_out0), .Q(Reg_0_q), .clk(Clock));  // open: clr
  Register #(.width(32), .trigger("falling")) Reg_1 (
    .D(Write_Data), .en(demultiplexer_1_out1), .Q(Reg_1_q), .clk(Clock));  // open: clr
  Register #(.width(32), .trigger("falling")) Reg_2 (
    .D(Write_Data), .en(demultiplexer_1_out2), .Q(Reg_2_q), .clk(Clock));  // open: clr
  Register #(.width(32), .trigger("falling")) Reg_3 (
    .D(Write_Data), .en(demultiplexer_1_out3), .Q(Reg_3_q), .clk(Clock));  // open: clr
  Register #(.width(32), .trigger("falling")) Reg_4 (
    .D(Write_Data), .en(demultiplexer_1_out4), .Q(Reg_4_q), .clk(Clock));  // open: clr
  Register #(.width(32), .trigger("falling")) Reg_5 (
    .D(Write_Data), .en(demultiplexer_1_out5), .Q(Reg_5_q), .clk(Clock));  // open: clr
  Register #(.width(32), .trigger("falling")) Reg_6 (
    .D(Write_Data), .en(demultiplexer_1_out6), .Q(Reg_6_q), .clk(Clock));  // open: clr
  Register #(.width(32), .trigger("falling")) Reg_7 (
    .D(Write_Data), .en(demultiplexer_1_out7), .Q(Reg_7_q), .clk(Clock));  // open: clr
  Register #(.width(32), .trigger("falling")) Reg_8 (
    .D(Write_Data), .en(demultiplexer_1_out8), .Q(Reg_8_q), .clk(Clock));  // open: clr
  Register #(.width(32), .trigger("falling")) Reg_9 (
    .D(Write_Data), .en(demultiplexer_1_out9), .Q(Reg_9_q), .clk(Clock));  // open: clr
  Register #(.width(32), .trigger("falling")) Reg_10 (
    .D(Write_Data), .en(demultiplexer_1_out10), .Q(Reg_10_q), .clk(Clock));  // open: clr
  Register #(.width(32), .trigger("falling")) Reg_11 (
    .D(Write_Data), .en(demultiplexer_1_out11), .Q(Reg_11_q), .clk(Clock));  // open: clr
  Register #(.width(32), .trigger("falling")) Reg_12 (
    .D(Write_Data), .en(demultiplexer_1_out12), .Q(Reg_12_q), .clk(Clock));  // open: clr
  Register #(.width(32), .trigger("falling")) Reg_13 (
    .D(Write_Data), .en(demultiplexer_1_out13), .Q(Reg_13_q), .clk(Clock));  // open: clr
  Register #(.width(32), .trigger("falling")) Reg_14 (
    .D(Write_Data), .en(demultiplexer_1_out14), .Q(Reg_14_q), .clk(Clock));  // open: clr
  Register #(.width(32), .trigger("falling")) Reg_15 (
    .D(Write_Data), .en(demultiplexer_1_out15), .Q(Reg_15_q), .clk(Clock));  // open: clr
  Register #(.width(32), .trigger("falling")) Reg_16 (
    .D(Write_Data), .en(demultiplexer_1_out16), .Q(Reg_16_q), .clk(Clock));  // open: clr
  Register #(.width(32), .trigger("falling")) Reg_17 (
    .D(Write_Data), .en(demultiplexer_1_out17), .Q(Reg_17_q), .clk(Clock));  // open: clr
  Register #(.width(32), .trigger("falling")) Reg_18 (
    .D(Write_Data), .en(demultiplexer_1_out18), .Q(Reg_18_q), .clk(Clock));  // open: clr
  Register #(.width(32), .trigger("falling")) Reg_19 (
    .D(Write_Data), .en(demultiplexer_1_out19), .Q(Reg_19_q), .clk(Clock));  // open: clr
  Register #(.width(32), .trigger("falling")) Reg_20 (
    .D(Write_Data), .en(demultiplexer_1_out20), .Q(Reg_20_q), .clk(Clock));  // open: clr
  Register #(.width(32), .trigger("falling")) Reg_21 (
    .D(Write_Data), .en(demultiplexer_1_out21), .Q(Reg_21_q), .clk(Clock));  // open: clr
  Register #(.width(32), .trigger("falling")) Reg_22 (
    .D(Write_Data), .en(demultiplexer_1_out22), .Q(Reg_22_q), .clk(Clock));  // open: clr
  Register #(.width(32), .trigger("falling")) Reg_23 (
    .D(Write_Data), .en(demultiplexer_1_out23), .Q(Reg_23_q), .clk(Clock));  // open: clr
  Register #(.width(32), .trigger("falling")) Reg_24__t8 (
    .D(Write_Data), .en(demultiplexer_1_out24), .Q(from__t8), .clk(Clock));  // open: clr
  Register #(.width(32), .trigger("falling")) Reg_25__t9 (
    .D(controlled_buffer_1_out), .en(controlled_buffer_2_out), .Q(from__t9), .clk(Clock));  // open: clr
  Register #(.width(32), .trigger("falling")) Reg_26 (
    .D(Write_Data), .en(demultiplexer_1_out26), .Q(Reg_26_q), .clk(Clock));  // open: clr
  Register #(.width(32), .trigger("falling")) Reg_27 (
    .D(Write_Data), .en(demultiplexer_1_out27), .Q(Reg_27_q), .clk(Clock));  // open: clr
  Register #(.width(32), .trigger("falling")) Reg_28 (
    .D(Write_Data), .en(demultiplexer_1_out28), .Q(Reg_28_q), .clk(Clock));  // open: clr
  Register #(.width(32), .trigger("falling")) Reg_29 (
    .D(Write_Data), .en(demultiplexer_1_out29), .Q(Reg_29_q), .clk(Clock));  // open: clr
  Register #(.width(32), .trigger("falling")) Reg_30 (
    .D(Write_Data), .en(demultiplexer_1_out30), .Q(Reg_30_q), .clk(Clock));  // open: clr
  Register #(.width(32), .trigger("falling")) Reg_31 (
    .D(Write_Data), .en(demultiplexer_1_out31), .Q(Reg_31_q), .clk(Clock));  // open: clr
  // Probe on Write_Data
  Multiplexer #(.select(5), .width(32)) multiplexer_1 (
    .in0(Reg_0_q), .in1(Reg_1_q), .in2(Reg_2_q), .in3(Reg_3_q), .in4(Reg_4_q), .in5(Reg_5_q), .in6(Reg_6_q),
    .in7(Reg_7_q), .in8(Reg_8_q), .in9(Reg_9_q), .in10(Reg_10_q), .in11(Reg_11_q), .in12(Reg_12_q),
    .in13(Reg_13_q), .in14(Reg_14_q), .in15(Reg_15_q), .in16(Reg_16_q), .in17(Reg_17_q), .in18(Reg_18_q),
    .in19(Reg_19_q), .in20(Reg_20_q), .in21(Reg_21_q), .in22(Reg_22_q), .in23(Reg_23_q), .in24(from__t8),
    .in25(from__t9), .in26(Reg_26_q), .in27(Reg_27_q), .in28(Reg_28_q), .in29(Reg_29_q), .in30(Reg_30_q),
    .in31(Reg_31_q), .out(Read_Data_1), .sel(Read_Register_1));  // open: en
  Multiplexer #(.select(5), .width(32)) multiplexer_2 (
    .in0(Reg_0_q), .in1(Reg_1_q), .in2(Reg_2_q), .in3(Reg_3_q), .in4(Reg_4_q), .in5(Reg_5_q), .in6(Reg_6_q),
    .in7(Reg_7_q), .in8(Reg_8_q), .in9(Reg_9_q), .in10(Reg_10_q), .in11(Reg_11_q), .in12(Reg_12_q),
    .in13(Reg_13_q), .in14(Reg_14_q), .in15(Reg_15_q), .in16(Reg_16_q), .in17(Reg_17_q), .in18(Reg_18_q),
    .in19(Reg_19_q), .in20(Reg_20_q), .in21(Reg_21_q), .in22(Reg_22_q), .in23(Reg_23_q), .in24(from__t8),
    .in25(from__t9), .in26(Reg_26_q), .in27(Reg_27_q), .in28(Reg_28_q), .in29(Reg_29_q), .in30(Reg_30_q),
    .in31(Reg_31_q), .out(Read_Data_2), .sel(Read_Register_2));  // open: en
endmodule

module Control_Unit__Done (
  input  [5:0] Opcode,
  output Jump,
  output RegDst,
  output Reg_Write,
  output ALU_SRC,
  output Branch_If_Equal,
  output [1:0] ALUOp,
  output Branch_if_NOT_Equal,
  output ADDI
);

  wire and_4_out, and_9_out, not_1_out, not_2_out, not_3_out, not_4_out, not_5_out, not_6_out, not_7_out,
       not_8_out, not_9_out, not_10_out, not_11_out, not_12_out, not_13_out, not_14_out, not_15_out,
       not_16_out, not_17_out, not_18_out, not_19_out, not_20_out, not_21_out, not_22_out, not_23_out,
       not_24_out, not_25_out, not_26_out, not_27_out, not_28_out, not_29_out, not_30_out, not_31_out,
       not_32_out, not_33_out, not_34_out, not_35_out, not_36_out, not_37_out, or_1_out;

  not not_1 (not_1_out, Opcode[1]);
  and and_1 (ADDI, not_1_out, not_2_out, not_4_out, not_5_out, Opcode[3]);
  not not_2 (not_2_out, Opcode[5]);
  not not_3 (not_3_out, Opcode[4]);
  not not_4 (not_4_out, Opcode[0]);
  not not_5 (not_5_out, Opcode[2]);
  not not_6 (not_6_out, Opcode[3]);
  and and_2 (Jump, Opcode[1], not_5_out, not_6_out, not_3_out, not_2_out);
  not not_7 (not_7_out, Opcode[0]);
  not not_8 (not_8_out, Opcode[4]);
  not not_9 (not_9_out, Opcode[1]);
  and and_3 (Branch_If_Equal, not_7_out, not_8_out, not_10_out, Opcode[2], not_11_out);
  and and_4 (and_4_out, Opcode[1], Opcode[3]);
  not not_10 (not_10_out, Opcode[5]);
  not not_11 (not_11_out, Opcode[3]);
  not not_12 (not_12_out, Opcode[2]);
  not not_13 (not_13_out, Opcode[0]);
  // AND_Gate and_5 has open pins: in0=not_13_out, in1=Opcode[1], in2=Opcode[5], in3=not_16_out, in4=not_17_out, out=open
  not not_14 (not_14_out, Opcode[5]);
  not not_15 (not_15_out, Opcode[3]);
  not not_16 (not_16_out, Opcode[3]);
  not not_17 (not_17_out, Opcode[4]);
  or or_1 (or_1_out, Branch_If_Equal, Branch_if_NOT_Equal);
  not not_18 (not_18_out, Opcode[2]);
  not not_19 (not_19_out, Opcode[4]);
  not not_20 (not_20_out, Opcode[5]);
  not not_21 (not_21_out, Opcode[3]);
  not not_22 (not_22_out, Opcode[1]);
  and and_6 (Branch_if_NOT_Equal, Opcode[0], not_22_out, Opcode[2], not_19_out, not_20_out);
  not not_23 (not_23_out, Branch_if_NOT_Equal);
  not not_24 (not_24_out, Opcode[4]);
  not not_25 (not_25_out, Opcode[3]);
  not not_26 (not_26_out, Opcode[2]);
  // AND_Gate and_7 has open pins: in0=not_18_out, in1=not_25_out, in2=not_24_out, in3=Opcode[1], in4=Opcode[0], in5=Opcode[5], out=open
  and and_8 (RegDst, not_14_out, not_15_out);
  not not_27 (not_27_out, Branch_If_Equal);
  not not_28 (not_28_out, Jump);
  or or_2 (ALUOp[0], or_1_out, and_4_out);
  not not_29 (not_29_out, Opcode[0]);
  not not_30 (not_30_out, Opcode[1]);
  not not_31 (not_31_out, Opcode[4]);
  not not_32 (not_32_out, Opcode[3]);
  not not_33 (not_33_out, Opcode[5]);
  and and_9 (and_9_out, not_26_out, not_32_out, not_31_out, not_30_out, not_29_out, not_33_out);
  and and_10 (Reg_Write, not_27_out, not_28_out, not_23_out);
  not not_34 (not_34_out, and_9_out);
  not not_35 (not_35_out, Branch_If_Equal);
  not not_36 (not_36_out, or_1_out);
  not not_37 (not_37_out, Jump);
  and and_11 (ALUOp[1], not_36_out, not_37_out);
  and and_12 (ALU_SRC, not_34_out, not_35_out, not_23_out);
endmodule

module Spare (
  input  [3:0] Op,
  input  [31:0] Input,
  input  [31:0] Input_2,
  output ZERO,
  output [31:0] out_5,
  output Overflow
);

  wire n8_bit_alu_1_overflow, n8_bit_alu_1_zero, n8_bit_alu_2_overflow, n8_bit_alu_2_zero,
       n8_bit_alu_3_overflow, n8_bit_alu_3_zero, n8_bit_alu_4_overflow, n8_bit_alu_4_zero;
  wire [1:0] undriven;

  _8_bit_ALU_part u_8_bit_alu_1 (
    .A(Input[7:0]), .B(Input_2[7:0]), .A_Invert(Op[3]), .BInvert(Op[2]), .OP(undriven),
    .Zero(n8_bit_alu_1_zero), .Result(out_5[7:0]), .Overflow(n8_bit_alu_1_overflow));
  _8_bit_ALU_part u_8_bit_alu_2 (
    .A(Input[15:8]), .B(Input_2[15:8]), .A_Invert(Op[3]), .BInvert(Op[2]), .OP(undriven),
    .Zero(n8_bit_alu_2_zero), .Result(out_5[15:8]), .Overflow(n8_bit_alu_2_overflow));
  _8_bit_ALU_part u_8_bit_alu_3 (
    .A(Input[23:16]), .B(Input_2[23:16]), .A_Invert(Op[3]), .BInvert(Op[2]), .OP(undriven),
    .Zero(n8_bit_alu_3_zero), .Result(out_5[23:16]), .Overflow(n8_bit_alu_3_overflow));
  _8_bit_ALU_part u_8_bit_alu_4 (
    .A(Input[31:24]), .B(Input_2[31:24]), .A_Invert(Op[3]), .BInvert(Op[2]), .OP(undriven),
    .Zero(n8_bit_alu_4_zero), .Result(out_5[31:24]), .Overflow(n8_bit_alu_4_overflow));
  // AND_Gate and_1 is placed but not wired
  or or_1 (ZERO, n8_bit_alu_1_zero, n8_bit_alu_2_zero, n8_bit_alu_3_zero, n8_bit_alu_4_zero);
  or or_2 (Overflow, n8_bit_alu_3_overflow, n8_bit_alu_1_overflow, n8_bit_alu_2_overflow, n8_bit_alu_4_overflow);
endmodule

module _8_bit_ALU (
  input  [7:0] A,
  input  [1:0] OP,
  input  A_Invert,
  input  BInvert,
  input  Carry_In,
  input  [7:0] B,
  input  Less,
  output [7:0] Result,
  output Set,
  output Carry_Out
);

  wire n1_bit_alu_1_carry_out, n1_bit_alu_2_carry_out, n1_bit_alu_4_carry_out, n1_bit_alu_5_carry_out,
       n1_bit_alu_6_carry_out, n1_bit_alu_7_carry_out, n1_bit_alu_8_carry_out;

  lab08_1_bit_ALU u_1_bit_alu_1 (
    .A(A[5]), .B(B[5]), .Less(1'b0), .Ainvert(A_Invert), .Binvert(BInvert), .CarryIn(n1_bit_alu_8_carry_out),
    .Operation(OP), .Carry_Out(n1_bit_alu_1_carry_out), .Result(Result[5]));  // open: Set
  lab08_1_bit_ALU u_1_bit_alu_2 (
    .A(A[6]), .B(B[6]), .Less(1'b0), .Ainvert(A_Invert), .Binvert(BInvert), .CarryIn(n1_bit_alu_1_carry_out),
    .Operation(OP), .Carry_Out(n1_bit_alu_2_carry_out), .Result(Result[6]));  // open: Set
  lab08_1_bit_ALU u_1_bit_alu_3 (
    .A(A[7]), .B(B[7]), .Less(1'b0), .Ainvert(A_Invert), .Binvert(BInvert), .CarryIn(n1_bit_alu_2_carry_out),
    .Operation(OP), .Carry_Out(Carry_Out), .Result(Result[7]), .Set(Set));
  lab08_1_bit_ALU u_1_bit_alu_4 (
    .A(A[0]), .B(B[0]), .Less(Less), .Ainvert(A_Invert), .Binvert(BInvert), .CarryIn(Carry_In),
    .Operation(OP), .Carry_Out(n1_bit_alu_4_carry_out), .Result(Result[0]));  // open: Set
  lab08_1_bit_ALU u_1_bit_alu_5 (
    .A(A[1]), .B(B[1]), .Less(1'b0), .Ainvert(A_Invert), .Binvert(BInvert), .CarryIn(n1_bit_alu_4_carry_out),
    .Operation(OP), .Carry_Out(n1_bit_alu_5_carry_out), .Result(Result[1]));  // open: Set
  lab08_1_bit_ALU u_1_bit_alu_6 (
    .A(A[2]), .B(B[2]), .Less(1'b0), .Ainvert(A_Invert), .Binvert(BInvert), .CarryIn(n1_bit_alu_5_carry_out),
    .Operation(OP), .Carry_Out(n1_bit_alu_6_carry_out), .Result(Result[2]));  // open: Set
  lab08_1_bit_ALU u_1_bit_alu_7 (
    .A(A[3]), .B(B[3]), .Less(1'b0), .Ainvert(A_Invert), .Binvert(BInvert), .CarryIn(n1_bit_alu_6_carry_out),
    .Operation(OP), .Carry_Out(n1_bit_alu_7_carry_out), .Result(Result[3]));  // open: Set
  lab08_1_bit_ALU u_1_bit_alu_8 (
    .A(A[4]), .B(B[4]), .Less(1'b0), .Ainvert(A_Invert), .Binvert(BInvert), .CarryIn(n1_bit_alu_7_carry_out),
    .Operation(OP), .Carry_Out(n1_bit_alu_8_carry_out), .Result(Result[4]));  // open: Set
  // lab08_1_bit_ALU 1_bit_alu_9: pin names not known
endmodule

module CPU (
  input  [31:0] Write_to__t9,
  input  Write_To_Keyboard,
  output [31:0] from__t8,
  output [31:0] from__t94
);

  wire and_1_out, and_2_out, clock_1_out, control_unit_done_1_addi, control_unit_done_1_alu_src,
       control_unit_done_1_branch_if_equal, control_unit_done_1_branch_if_not_equal,
       control_unit_done_1_jump, control_unit_done_1_reg_write, control_unit_done_1_regdst,
       n32_bit_alu_done_1_zero, not_1_out, or_1_out;
  wire [1:0] alu_control_unit_1_shift_amount, control_unit_done_1_aluop;
  wire [3:0] alu_control_unit_1_out_3, multiplexer_3_out;
  wire [4:0] multiplexer_1_out;
  wire [25:0] shifter_1_out;
  wire [31:0] adder_1_out, adder_2_out, instruction_memory_done_1_out_2, multiplexer_2_out,
       multiplexer_4_out, multiplexer_5_out, n32_bit_alu_done_1_result, register_1_q,
       register_file_finish_t8_t9_1_read_data_1, register_file_finish_t8_t9_1_read_data_2, shifter_2_out,
       sign_extend_1_out_2;

  // Probe on multiplexer_5_out
  Register #(.width(32)) register_1 (.D(multiplexer_5_out), .Q(register_1_q), .clk(clock_1_out));  // open: en, clr
  Adder #(.width(32)) adder_1 (.a(register_1_q), .b(32'h4), .out(adder_1_out));  // open: cin, cout
  // Probe on instruction_memory_done_1_out_2
  // Probe on nothing
  Instruction_Memory__Done instruction_memory_done_1 (
    .Adress(register_1_q[17:2]), .out_2(instruction_memory_done_1_out_2));
  Shifter #(.width(26)) shifter_1 (.in(instruction_memory_done_1_out_2[25:0]), .\dist (5'b00010), .out(shifter_1_out));
  Control_Unit__Done control_unit_done_1 (
    .Opcode(instruction_memory_done_1_out_2[31:26]), .Jump(control_unit_done_1_jump),
    .RegDst(control_unit_done_1_regdst), .Reg_Write(control_unit_done_1_reg_write),
    .ALU_SRC(control_unit_done_1_alu_src), .Branch_If_Equal(control_unit_done_1_branch_if_equal),
    .ALUOp(control_unit_done_1_aluop), .Branch_if_NOT_Equal(control_unit_done_1_branch_if_not_equal),
    .ADDI(control_unit_done_1_addi));
  Multiplexer #(.width(5)) multiplexer_1 (
    .in0(instruction_memory_done_1_out_2[20:16]), .in1(instruction_memory_done_1_out_2[15:11]),
    .out(multiplexer_1_out), .sel(control_unit_done_1_regdst));  // open: en
  Clock clock_1 (.out(clock_1_out));
  Register_File__Finish__t8___t9 register_file_finish_t8_t9_1 (
    .Write(control_unit_done_1_reg_write), .Write_Register(multiplexer_1_out),
    .Write_Data(n32_bit_alu_done_1_result), .Read_Register_1(instruction_memory_done_1_out_2[25:21]),
    .Read_Register_2(instruction_memory_done_1_out_2[20:16]), .Write_to__t9(Write_to__t9),
    .Write_Signal_From_Keypad(Write_To_Keyboard), .Clock(clock_1_out),
    .Read_Data_1(register_file_finish_t8_t9_1_read_data_1),
    .Read_Data_2(register_file_finish_t8_t9_1_read_data_2), .from__t8(from__t8), .from__t9(from__t94));
  Sign_Extend sign_extend_1 (.Input(instruction_memory_done_1_out_2[15:0]), .out_2(sign_extend_1_out_2));
  Shifter #(.width(32)) shifter_2 (.in(sign_extend_1_out_2), .\dist (5'b00010), .out(shifter_2_out));
  Multiplexer #(.width(32)) multiplexer_2 (
    .in0(register_file_finish_t8_t9_1_read_data_2), .in1(sign_extend_1_out_2), .out(multiplexer_2_out),
    .sel(control_unit_done_1_alu_src));  // open: en
  Adder #(.width(32)) adder_2 (.a(adder_1_out), .b(shifter_2_out), .out(adder_2_out));  // open: cin, cout
  // Probe on n32_bit_alu_done_1_result
  _32_bit_ALU__Done u_32_bit_alu_done_1 (
    .A_Input(register_file_finish_t8_t9_1_read_data_1), .B_Input(multiplexer_2_out),
    .Shift_Amount(instruction_memory_done_1_out_2[10:6]), .A_Invert(multiplexer_3_out[3]),
    .BInvert(multiplexer_3_out[2]), .OP(multiplexer_3_out[1:0]),
    .Shift_Control(alu_control_unit_1_shift_amount), .Zero(n32_bit_alu_done_1_zero),
    .Result(n32_bit_alu_done_1_result));  // open: Overflow
  ALU_Control_Unit alu_control_unit_1 (
    .Funct(instruction_memory_done_1_out_2[5:0]), .ALU_Op(control_unit_done_1_aluop),
    .out_3(alu_control_unit_1_out_3), .Shift_Amount(alu_control_unit_1_shift_amount));
  Multiplexer #(.width(4)) multiplexer_3 (
    .in0(alu_control_unit_1_out_3), .in1(4'b0010), .out(multiplexer_3_out), .sel(control_unit_done_1_addi));  // open: en
  Multiplexer #(.width(32)) multiplexer_4 (
    .in0(adder_1_out), .in1(adder_2_out), .out(multiplexer_4_out), .sel(or_1_out));  // open: en
  and and_1 (and_1_out, control_unit_done_1_branch_if_not_equal, not_1_out);
  Multiplexer #(.width(32)) multiplexer_5 (
    .in0(multiplexer_4_out), .in1({adder_1_out[31:26], shifter_1_out}), .out(multiplexer_5_out),
    .sel(control_unit_done_1_jump));  // open: en
  or or_1 (or_1_out, and_1_out, and_2_out);
  and and_2 (and_2_out, control_unit_done_1_branch_if_equal, n32_bit_alu_done_1_zero);
  not not_1 (not_1_out, n32_bit_alu_done_1_zero);
endmodule

module Backup_ALU__without_SLT (
  input  [1:0] OpCode,
  input  A_invert,
  input  B_invert,
  input  [31:0] Input,
  input  [31:0] Input_2,
  output [31:0] out_6
);

  wire [31:0] adder_1_out, and_1_out, and_2_out, multiplexer_1_out, multiplexer_2_out, not_1_out, not_2_out;

  assign not_1_out = ~Input;  // NOT_Gate not_1, 32 bits wide
  assign not_2_out = ~Input_2;  // NOT_Gate not_2, 32 bits wide
  Multiplexer #(.width(32)) multiplexer_1 (
    .in0(Input), .in1(not_1_out), .out(multiplexer_1_out), .sel(A_invert));  // open: en
  Multiplexer #(.width(32)) multiplexer_2 (
    .in0(Input_2), .in1(not_2_out), .out(multiplexer_2_out), .sel(B_invert));  // open: en
  assign and_1_out = multiplexer_2_out & multiplexer_1_out;  // AND_Gate and_1, 32 bits wide
  assign and_2_out = multiplexer_1_out & multiplexer_2_out;  // AND_Gate and_2, 32 bits wide
  Adder #(.width(32)) adder_1 (.a(multiplexer_1_out), .b(multiplexer_2_out), .out(adder_1_out));  // open: cin, cout
  Multiplexer #(.select(2), .width(32)) multiplexer_3 (
    .in1(and_1_out), .in2(and_2_out), .in3(adder_1_out), .out(out_6), .sel(OpCode));  // open: in0, en
endmodule

module Register_File (
  input  Write,
  input  [4:0] Read_Register_1,
  input  [4:0] Read_Register_2,
  input  [4:0] Write_Register,
  output [31:0] Read_Data_1,
  output [31:0] Read_Data_2
);

  wire and_1_out, and_2_out, and_3_out, and_4_out, and_5_out, and_6_out, and_7_out, and_8_out, and_9_out,
       and_10_out, and_11_out, and_12_out, and_13_out, and_14_out, and_15_out, and_16_out, and_17_out,
       and_18_out, and_19_out, and_20_out, and_21_out, and_22_out, and_23_out, and_24_out, and_25_out,
       and_26_out, and_27_out, and_28_out, and_29_out, and_30_out, and_31_out, and_32_out, decoder_1_out0,
       decoder_1_out1, decoder_1_out2, decoder_1_out3, decoder_1_out4, decoder_1_out5, decoder_1_out6,
       decoder_1_out7, decoder_1_out8, decoder_1_out9, decoder_1_out10, decoder_1_out11, decoder_1_out12,
       decoder_1_out13, decoder_1_out14, decoder_1_out15, decoder_1_out16, decoder_1_out17, decoder_1_out18,
       decoder_1_out19, decoder_1_out20, decoder_1_out21, decoder_1_out22, decoder_1_out23, decoder_1_out24,
       decoder_1_out25, decoder_1_out26, decoder_1_out27, decoder_1_out28, decoder_1_out29, decoder_1_out30,
       decoder_1_out31;
  wire [31:0] Reg_0_q, Reg_1_q, Reg_2_q, Reg_3_q, Reg_4_q, Reg_5_q, Reg_6_q, Reg_7_q, Reg_8_q, Reg_9_q,
       Reg_10_q, Reg_11_q, Reg_12_q, Reg_13_q, Reg_14_q, Reg_15_q, Reg_16_q, Reg_17_q, Reg_18_q, Reg_19_q,
       Reg_20_q, Reg_21_q, Reg_22_q, Reg_23_q, Reg_24_q, Reg_25_q, Reg_26_q, Reg_27_q, Reg_28_q, Reg_29_q,
       Reg_30_q, Reg_31_q;

  Decoder #(.select(5)) decoder_1 (
    .out0(decoder_1_out0), .out1(decoder_1_out1), .out2(decoder_1_out2), .out3(decoder_1_out3),
    .out4(decoder_1_out4), .out5(decoder_1_out5), .out6(decoder_1_out6), .out7(decoder_1_out7),
    .out8(decoder_1_out8), .out9(decoder_1_out9), .out10(decoder_1_out10), .out11(decoder_1_out11),
    .out12(decoder_1_out12), .out13(decoder_1_out13), .out14(decoder_1_out14), .out15(decoder_1_out15),
    .out16(decoder_1_out16), .out17(decoder_1_out17), .out18(decoder_1_out18), .out19(decoder_1_out19),
    .out20(decoder_1_out20), .out21(decoder_1_out21), .out22(decoder_1_out22), .out23(decoder_1_out23),
    .out24(decoder_1_out24), .out25(decoder_1_out25), .out26(decoder_1_out26), .out27(decoder_1_out27),
    .out28(decoder_1_out28), .out29(decoder_1_out29), .out30(decoder_1_out30), .out31(decoder_1_out31),
    .sel(Write_Register));  // open: en
  and and_1 (and_1_out, Write, decoder_1_out0);
  and and_2 (and_2_out, decoder_1_out1, Write);
  and and_3 (and_3_out, decoder_1_out2, Write);
  and and_4 (and_4_out, decoder_1_out3, Write);
  and and_5 (and_5_out, decoder_1_out4, Write);
  and and_6 (and_6_out, decoder_1_out5, Write);
  and and_7 (and_7_out, decoder_1_out6, Write);
  and and_8 (and_8_out, decoder_1_out7, Write);
  and and_9 (and_9_out, decoder_1_out8, Write);
  and and_10 (and_10_out, Write, decoder_1_out9);
  and and_11 (and_11_out, Write, decoder_1_out10);
  and and_12 (and_12_out, Write, decoder_1_out11);
  and and_13 (and_13_out, Write, decoder_1_out12);
  and and_14 (and_14_out, decoder_1_out13, Write);
  and and_15 (and_15_out, Write, decoder_1_out14);
  and and_16 (and_16_out, Write, decoder_1_out15);
  and and_17 (and_17_out, Write, decoder_1_out16);
  and and_18 (and_18_out, Write, decoder_1_out17);
  and and_19 (and_19_out, decoder_1_out18, Write);
  and and_20 (and_20_out, Write, decoder_1_out19);
  and and_21 (and_21_out, Write, decoder_1_out20);
  and and_22 (and_22_out, Write, decoder_1_out21);
  and and_23 (and_23_out, decoder_1_out22, Write);
  and and_24 (and_24_out, Write, decoder_1_out23);
  and and_25 (and_25_out, Write, decoder_1_out24);
  and and_26 (and_26_out, decoder_1_out25, Write);
  and and_27 (and_27_out, Write, decoder_1_out26);
  and and_28 (and_28_out, decoder_1_out27, Write);
  and and_29 (and_29_out, Write, decoder_1_out28);
  and and_30 (and_30_out, decoder_1_out29, Write);
  and and_31 (and_31_out, decoder_1_out30, Write);
  and and_32 (and_32_out, decoder_1_out31, Write);
  Register #(.width(32), .trigger("falling")) Reg_0 (.en(and_1_out), .Q(Reg_0_q), .clk(Write));  // open: D, clr
  Register #(.width(32), .trigger("falling")) Reg_1 (.en(and_2_out), .Q(Reg_1_q), .clk(Write));  // open: D, clr
  Register #(.width(32), .trigger("falling")) Reg_2 (.en(and_3_out), .Q(Reg_2_q), .clk(Write));  // open: D, clr
  Register #(.width(32), .trigger("falling")) Reg_3 (.en(and_4_out), .Q(Reg_3_q), .clk(Write));  // open: D, clr
  Register #(.width(32), .trigger("falling")) Reg_4 (.en(and_5_out), .Q(Reg_4_q), .clk(Write));  // open: D, clr
  Register #(.width(32), .trigger("falling")) Reg_5 (.en(and_6_out), .Q(Reg_5_q), .clk(Write));  // open: D, clr
  Register #(.width(32), .trigger("falling")) Reg_6 (.en(and_7_out), .Q(Reg_6_q), .clk(Write));  // open: D, clr
  Register #(.width(32), .trigger("falling")) Reg_7 (.en(and_8_out), .Q(Reg_7_q), .clk(Write));  // open: D, clr
  Register #(.width(32), .trigger("falling")) Reg_8 (.en(and_9_out), .Q(Reg_8_q), .clk(Write));  // open: D, clr
  Register #(.width(32), .trigger("falling")) Reg_9 (.en(and_10_out), .Q(Reg_9_q), .clk(Write));  // open: D, clr
  Register #(.width(32), .trigger("falling")) Reg_10 (.en(and_11_out), .Q(Reg_10_q), .clk(Write));  // open: D, clr
  Register #(.width(32), .trigger("falling")) Reg_11 (.en(and_12_out), .Q(Reg_11_q), .clk(Write));  // open: D, clr
  Register #(.width(32), .trigger("falling")) Reg_12 (.en(and_13_out), .Q(Reg_12_q), .clk(Write));  // open: D, clr
  Register #(.width(32), .trigger("falling")) Reg_13 (.en(and_14_out), .Q(Reg_13_q), .clk(Write));  // open: D, clr
  Register #(.width(32), .trigger("falling")) Reg_14 (.en(and_15_out), .Q(Reg_14_q), .clk(Write));  // open: D, clr
  Register #(.width(32), .trigger("falling")) Reg_15 (.en(and_16_out), .Q(Reg_15_q), .clk(Write));  // open: D, clr
  Register #(.width(32), .trigger("falling")) Reg_16 (.en(and_17_out), .Q(Reg_16_q), .clk(Write));  // open: D, clr
  Register #(.width(32), .trigger("falling")) Reg_17 (.en(and_18_out), .Q(Reg_17_q), .clk(Write));  // open: D, clr
  Register #(.width(32), .trigger("falling")) Reg_18 (.en(and_19_out), .Q(Reg_18_q), .clk(Write));  // open: D, clr
  Register #(.width(32), .trigger("falling")) Reg_19 (.en(and_20_out), .Q(Reg_19_q), .clk(Write));  // open: D, clr
  Register #(.width(32), .trigger("falling")) Reg_20 (.en(and_21_out), .Q(Reg_20_q));  // open: D, clk, clr
  Register #(.width(32), .trigger("falling")) Reg_21 (.en(and_22_out), .Q(Reg_21_q), .clk(Write));  // open: D, clr
  Register #(.width(32), .trigger("falling")) Reg_22 (.en(and_23_out), .Q(Reg_22_q), .clk(Write));  // open: D, clr
  Register #(.width(32), .trigger("falling")) Reg_23 (.en(and_24_out), .Q(Reg_23_q), .clk(Write));  // open: D, clr
  Register #(.width(32), .trigger("falling")) Reg_24 (.en(and_25_out), .Q(Reg_24_q), .clk(Write));  // open: D, clr
  Register #(.width(32), .trigger("falling")) Reg_25 (.en(and_26_out), .Q(Reg_25_q), .clk(Write));  // open: D, clr
  Register #(.width(32), .trigger("falling")) Reg_26 (.en(and_27_out), .Q(Reg_26_q), .clk(Write));  // open: D, clr
  Register #(.width(32), .trigger("falling")) Reg_27 (.en(and_28_out), .Q(Reg_27_q), .clk(Write));  // open: D, clr
  Register #(.width(32), .trigger("falling")) Reg_28 (.en(and_29_out), .Q(Reg_28_q), .clk(Write));  // open: D, clr
  Register #(.width(32), .trigger("falling")) Reg_29 (.en(and_30_out), .Q(Reg_29_q), .clk(Write));  // open: D, clr
  Register #(.width(32), .trigger("falling")) Reg_30 (.en(and_31_out), .Q(Reg_30_q), .clk(Write));  // open: D, clr
  Register #(.width(32), .trigger("falling")) Reg_31 (.en(and_32_out), .Q(Reg_31_q), .clk(Write));  // open: D, clr
  Multiplexer #(.select(5), .width(32)) multiplexer_1 (
    .in0(Reg_0_q), .in1(Reg_1_q), .in2(Reg_2_q), .in3(Reg_3_q), .in4(Reg_4_q), .in5(Reg_5_q), .in6(Reg_6_q),
    .in7(Reg_7_q), .in8(Reg_8_q), .in9(Reg_9_q), .in10(Reg_10_q), .in11(Reg_11_q), .in12(Reg_12_q),
    .in13(Reg_13_q), .in14(Reg_14_q), .in15(Reg_15_q), .in16(Reg_16_q), .in17(Reg_17_q), .in18(Reg_18_q),
    .in19(Reg_19_q), .in20(Reg_20_q), .in21(Reg_21_q), .in22(Reg_22_q), .in23(Reg_23_q), .in24(Reg_24_q),
    .in25(Reg_25_q), .in26(Reg_26_q), .in27(Reg_27_q), .in28(Reg_28_q), .in29(Reg_29_q), .in30(Reg_30_q),
    .in31(Reg_31_q), .out(Read_Data_1), .sel(Read_Register_1));  // open: en
  Multiplexer #(.select(5), .width(32)) multiplexer_2 (
    .in0(Reg_0_q), .in1(Reg_1_q), .in2(Reg_2_q), .in3(Reg_3_q), .in4(Reg_4_q), .in5(Reg_5_q), .in6(Reg_6_q),
    .in7(Reg_7_q), .in8(Reg_8_q), .in9(Reg_9_q), .in10(Reg_10_q), .in11(Reg_11_q), .in12(Reg_12_q),
    .in13(Reg_13_q), .in14(Reg_14_q), .in15(Reg_15_q), .in16(Reg_16_q), .in17(Reg_17_q), .in18(Reg_18_q),
    .in19(Reg_19_q), .in20(Reg_20_q), .in21(Reg_21_q), .in22(Reg_22_q), .in23(Reg_23_q), .in24(Reg_24_q),
    .in25(Reg_25_q), .in26(Reg_26_q), .in27(Reg_27_q), .in28(Reg_28_q), .in29(Reg_29_q), .in30(Reg_30_q),
    .in31(Reg_31_q), .out(Read_Data_2));  // open: sel, en
endmodule

module ALU_Control_Unit (
  input  [5:0] Funct,
  input  [1:0] ALU_Op,
  output [3:0] out_3,
  output [1:0] Shift_Amount
);

  wire [3:0] funct_control_1_opcode;

  funct_Control funct_control_1 (.Funct_Input(Funct), .OpCode(funct_control_1_opcode), .Shift_Control(Shift_Amount));
  Multiplexer #(.select(2), .width(4)) multiplexer_1 (
    .in0(4'b0010), .in1(4'b0110), .in2(funct_control_1_opcode), .in3(4'b0111), .out(out_3), .sel(ALU_Op));  // open: en
endmodule

module Sign_Extend (
  input  [15:0] Input,
  output [31:0] out_2
);


  assign out_2 = {{17{Input[15]}}, Input[14:0]};
endmodule

module funct_Control (
  input  [5:0] Funct_Input,
  output [3:0] OpCode,
  output [1:0] Shift_Control
);

  wire not_1_out, not_2_out, not_3_out, not_4_out, not_5_out, not_6_out, not_7_out, not_8_out, not_9_out,
       not_10_out, not_11_out, not_12_out;
  wire [0:0] and_1_out;
  wire [1:1] and_2_out;

  not not_1 (not_1_out, Funct_Input[4]);
  not not_2 (not_2_out, Funct_Input[5]);
  not not_3 (not_3_out, Funct_Input[0]);
  not not_4 (not_4_out, Funct_Input[2]);
  not not_5 (not_5_out, Funct_Input[3]);
  not not_6 (not_6_out, Funct_Input[2]);
  not not_7 (not_7_out, Funct_Input[1]);
  not not_8 (not_8_out, Funct_Input[0]);
  not not_9 (not_9_out, Funct_Input[3]);
  and and_1 (and_1_out[0], not_2_out, not_1_out, not_7_out, not_6_out, not_9_out);
  not not_10 (not_10_out, Funct_Input[2]);
  not not_11 (not_11_out, Funct_Input[4]);
  not not_12 (not_12_out, Funct_Input[5]);
  and and_2 (and_2_out[1], not_4_out, not_5_out, not_3_out, not_12_out, Funct_Input[1]);
  and and_3 (OpCode[1], not_10_out, Funct_Input[5]);
  and and_4 (OpCode[2], Funct_Input[1], Funct_Input[5]);
  or or_1 (OpCode[0], Funct_Input[0], Funct_Input[3]);
  assign Shift_Control = {1'b0, and_1_out[0]} | {and_2_out[1], 1'b0};  // OR_Gate or_2, 2 bits wide

  assign OpCode[3] = 1'b0;
endmodule

module _1_bit_ALU (
  input  Ainvert,
  input  Binvert,
  input  CarryIn,
  input  [1:0] Operation,
  input  A,
  input  B,
  input  Less,
  output Result,
  output Set,
  output Carry_Out
);

  wire and_1_out, multiplexer_1_out, multiplexer_2_out, not_1_out, not_2_out, or_1_out;

  not not_1 (not_1_out, A);
  not not_2 (not_2_out, B);
  Multiplexer multiplexer_1 (.in0(A), .in1(not_1_out), .out(multiplexer_1_out), .sel(Ainvert));  // open: en
  Multiplexer multiplexer_2 (.in0(B), .in1(not_2_out), .out(multiplexer_2_out), .sel(Binvert));  // open: en
  and and_1 (and_1_out, multiplexer_1_out, multiplexer_2_out);
  or or_1 (or_1_out, multiplexer_2_out, multiplexer_1_out);
  Adder #(.width(1)) adder_1 (.a(multiplexer_1_out), .b(multiplexer_2_out), .out(Set), .cin(CarryIn), .cout(Carry_Out));
  Multiplexer #(.select(2)) multiplexer_3 (
    .in0(and_1_out), .in1(or_1_out), .in2(Set), .in3(Less), .out(Result), .sel(Operation));  // open: en
endmodule
