// Logisim project lab08.circ as structural Verilog: 3 circuits, main circuit main
module main (
  input  [3:0] OpCode,
  input  [7:0] A,
  input  [7:0] B,
  output Zero,
  output [7:0] Result,
  output Overflow
);

  _8_bit_ALU u_8_bit_alu_1 (
    .A(A), .B(B), .A_Invert(OpCode[3]), .BInvert(OpCode[2]), .OP(OpCode[1:0]), .Zero(Zero), .Result(Result),
    .Overflow(Overflow));
endmodule

module _1_bit_ALU (
  input  Ainvert,
  input  Binvert,
  input  CarryIn,
  input  [1:0] Operation,
  input  A,
  input  B,
  input  Less,
  output Result,
  output Set,
  output Carry_Out
);

  wire and_1_out, multiplexer_1_out, multiplexer_2_out, not_1_out, not_2_out, or_1_out;

  not not_1 (not_1_out, A);
  not not_2 (not_2_out, B);
  Multiplexer multiplexer_1 (.in0(A), .in1(not_1_out), .out(multiplexer_1_out), .sel(Ainvert));  // open: en
  Multiplexer multiplexer_2 (.in0(B), .in1(not_2_out), .out(multiplexer_2_out), .sel(Binvert));  // open: en
  and and_1 (and_1_out, multiplexer_1_out, multiplexer_2_out);
  or or_1 (or_1_out, multiplexer_2_out, multiplexer_1_out);
  Adder #(.width(1)) adder_1 (.a(multiplexer_1_out), .b(multiplexer_2_out), .out(Set), .cin(CarryIn), .cout(Carry_Out));
  Multiplexer #(.select(2)) multiplexer_3 (
    .in0(and_1_out), .in1(or_1_out), .in2(Set), .in3(Less), .out(Result), .sel(Operation));  // open: en
endmodule

module _8_bit_ALU (
  input  [7:0] A,
  input  [1:0] OP,
  input  A_Invert,
  input  BInvert,
  input  [7:0] B,
  output Zero,
  output [7:0] Result,
  output Overflow
);

  wire n1_bit_alu_1_carry_out, n1_bit_alu_2_carry_out, n1_bit_alu_3_set, n1_bit_alu_4_carry_out,
       n1_bit_alu_5_carry_out, n1_bit_alu_6_carry_out, n1_bit_alu_7_carry_out, n1_bit_alu_8_carry_out,
       or_1_out, xor_1_out;

  _1_bit_ALU u_1_bit_alu_1 (
    .A(A[5]), .B(B[5]), .Less(1'b0), .Ainvert(A_Invert), .Binvert(BInvert), .CarryIn(n1_bit_alu_8_carry_out),
    .Operation(OP), .Carry_Out(n1_bit_alu_1_carry_out), .Result(Result[5]));  // open: Set
  _1_bit_ALU u_1_bit_alu_2 (
    .A(A[6]), .B(B[6]), .Less(1'b0), .Ainvert(A_Invert), .Binvert(BInvert), .CarryIn(n1_bit_alu_1_carry_out),
    .Operation(OP), .Carry_Out(n1_bit_alu_2_carry_out), .Result(Result[6]));  // open: Set
  _1_bit_ALU u_1_bit_alu_3 (
    .A(A[7]), .B(B[7]), .Less(1'b0), .Ainvert(A_Invert), .Binvert(BInvert), .CarryIn(n1_bit_alu_2_carry_out),
    .Operation(OP), .Carry_Out(Overflow), .Result(Result[7]), .Set(n1_bit_alu_3_set));
  _1_bit_ALU u_1_bit_alu_4 (
    .A(A[0]), .B(B[0]), .Less(xor_1_out), .Ainvert(A_Invert), .Binvert(BInvert), .CarryIn(BInvert),
    .Operation(OP), .Carry_Out(n1_bit_alu_4_carry_out), .Result(Result[0]));  // open: Set
  _1_bit_ALU u_1_bit_alu_5 (
    .A(A[1]), .B(B[1]), .Less(1'b0), .Ainvert(A_Invert), .Binvert(BInvert), .CarryIn(n1_bit_alu_4_carry_out),
    .Operation(OP), .Carry_Out(n1_bit_alu_5_carry_out), .Result(Result[1]));  // open: Set
  _1_bit_ALU u_1_bit_alu_6 (
    .A(A[2]), .B(B[2]), .Less(1'b0), .Ainvert(A_Invert), .Binvert(BInvert), .CarryIn(n1_bit_alu_5_carry_out),
    .Operation(OP), .Carry_Out(n1_bit_alu_6_carry_out), .Result(Result[2]));  // open: Set
  _1_bit_ALU u_1_bit_alu_7 (
    .A(A[3]), .B(B[3]), .Less(1'b0), .Ainvert(A_Invert), .Binvert(BInvert), .CarryIn(n1_bit_alu_6_carry_out),
    .Operation(OP), .Carry_Out(n1_bit_alu_7_carry_out), .Result(Result[3]));  // open: Set
  _1_bit_ALU u_1_bit_alu_8 (
    .A(A[4]), .B(B[4]), .Less(1'b0), .Ainvert(A_Invert), .Binvert(BInvert), .CarryIn(n1_bit_alu_7_carry_out),
    .Operation(OP), .Carry_Out(n1_bit_alu_8_carry_out), .Result(Result[4]));  // open: Set
  xor xor_1 (xor_1_out, n1_bit_alu_3_set, Overflow);
  not not_1 (Zero, or_1_out);
  or or_1 (or_1_out, Result[0], Result[1], Result[2], Result[3], Result[4], Result[5], Result[6], Result[7]);
endmodule
